# Fritzing sketch Final Board (saved by Fritzing 0.9.2b)
breadboards: 2

parts:
  U1 = CNZ1120 [package=cnz1120]
  U2 = CNZ1120 [package=cnz1120]
  R2 = Resistor [tolerance=±5% resistance=220 package=THT]
  R1 = Resistor [tolerance=±5% resistance=220 package=THT]
  R7 = Resistor [tolerance=±5% resistance=220 package=THT]
  R5 = Resistor [tolerance=±5% resistance=220 package=THT]
  R6 = Resistor [tolerance=±5% resistance=220 package=THT]
  NEOPIXEL1 = Neopixel Strip -- White (30/m)
  NEOPIXEL0 = Neopixel Strip -- White (30/m)
  NEOPIXEL11 = Neopixel Strip -- White (30/m)
  NEOPIXEL10 = Neopixel Strip -- White (30/m)
  NEOPIXEL9 = Neopixel Strip -- White (30/m)
  NEOPIXEL3 = Neopixel Strip -- White (30/m)
  NEOPIXEL4 = Neopixel Strip -- White (30/m)
  NEOPIXEL7 = Neopixel Strip -- White (30/m)
  NEOPIXEL8 = Neopixel Strip -- White (30/m)
  NEOPIXEL2 = Neopixel Strip -- White (30/m)
  NEOPIXEL6 = Neopixel Strip -- White (30/m)
  NEOPIXEL5 = Neopixel Strip -- White (30/m)
  C1 = Electrolytic Capacitor [capacitance=22µF package="1010 [SMD, electrolytic]"]
  R10 = Resistor [tolerance=±5% resistance=220 package=THT]
  R9 = Resistor [tolerance=±5% resistance=220 package=THT]
  R8 = Resistor [tolerance=±5% resistance=220 package=THT]
  R4 = Resistor [tolerance=±5% resistance=10k package="0402 [SMD]"]
  R3 = Resistor [tolerance=±5% resistance=10k package="0402 [SMD]"]
  ARDUINO = Arduino Micro
  JACK = 2.1mm Barrel Jack with Terminal Block

nets:
  N1: U1.1, R1.Pin_0
  GND: U1.2, U2.2, NEOPIXEL1.GND, NEOPIXEL0.GND, NEOPIXEL11.GND, NEOPIXEL10.GND, NEOPIXEL9.GND, NEOPIXEL3.GND, NEOPIXEL4.GND, NEOPIXEL7.GND, NEOPIXEL8.GND, NEOPIXEL2.GND, NEOPIXEL6.GND, NEOPIXEL5.GND, C1.-, R4.Pin_0, R3.Pin_0, ARDUINO.GND#31, JACK.NEG
  +5V: U1.3, U2.3, R2.Pin_1, R1.Pin_1, NEOPIXEL1.+5V, NEOPIXEL0.+5V, NEOPIXEL11.+5V, NEOPIXEL10.+5V, NEOPIXEL9.+5V, NEOPIXEL3.+5V, NEOPIXEL4.+5V, NEOPIXEL7.+5V, NEOPIXEL8.+5V, NEOPIXEL2.+5V, NEOPIXEL6.+5V, NEOPIXEL5.+5V, C1.+, ARDUINO.VIN, JACK.POS
  N2: U1.4, R4.Pin_1, ARDUINO.D3
  N3: U2.1, R2.Pin_0
  N4: U2.4, R3.Pin_1, ARDUINO.D2
  N5: R7.Pin_0, ARDUINO.D8
  N6: R7.Pin_1, NEOPIXEL4.Din, NEOPIXEL5.Din
  N7: R5.Pin_0, ARDUINO.D10
  N8: R5.Pin_1, NEOPIXEL1.Din, NEOPIXEL0.Din
  N9: R6.Pin_0, ARDUINO.D9
  N10: R6.Pin_1, NEOPIXEL3.Din, NEOPIXEL2.Din
  N11: NEOPIXEL11.Din, NEOPIXEL10.Din, R10.Pin_0
  N12: NEOPIXEL9.Din, NEOPIXEL8.Din, R9.Pin_0
  N13: NEOPIXEL7.Din, NEOPIXEL6.Din, R8.Pin_0
  N14: R10.Pin_1, ARDUINO.D5
  N15: R9.Pin_1, ARDUINO.D6
  N16: R8.Pin_1, ARDUINO.D7

custom parts:
  Neopixel Strip -- White (30/m): These NeoPixel strips have 30 digitally-addressable pixel LEDs per meter and are very affordable and are only 12.5 mm wide, 10 mm if you remove the strip from the casing.
  Arduino Micro: Arduino Micro Microcontroller
